# Fritzing sketch yarn dyer (saved by Fritzing 0.9.2b)
breadboards: 1

parts:
  Part1 = Arduino Uno (Rev3)
  U1 = LCD-16X2 [package=lcd-16x2]
  T1 = LM35 Temperature Sensor [package="TO92 [THT]"]
  LED1 = LED - 5mm [color="Red (633nm)" package="5 mm [THT]"]
  S1 = Pushbutton [package="[THT]"]
  R1 = Trimmer Potentiometer [maximum_resistance=10kΩ package=THT]
  R2 = Resistor [tolerance=±5% resistance=10k package=THT]
  R3 = Resistor [tolerance=±5% resistance=10k package=THT]
  R4 = Resistor [tolerance=±5% resistance=10k package=THT]
  R5 = Resistor [tolerance=±5% resistance=220 package=THT]
  RE1 = Rotary Encoder [package=THT]

nets:
  N1: Part1.D8, U1.E
  N2: Part1.D9_PWM, U1.DB4
  N3: Part1.D10_PWM/SS, U1.DB5
  N4: Part1.D11_PWM/MOSI, U1.DB6
  N5: Part1.D12/MISO, U1.DB7
  N6: Part1.D0/RX, T1.Vout
  N7: Part1.D1/TX, R5.Pin_0
  N8: Part1.D2, RE1.EncoderPinB
  N9: Part1.D3_PWM, R4.Pin_1, RE1.EncoderPinA
  N10: Part1.D4, S1.Pin_1, S1.Pin_2, R2.Pin_1
  N11: Part1.D7, U1.RS
  5V: Part1.5V, U1.VDD, U1.A, T1.+Vs, R1.leg1, R2.Pin_0, R3.Pin_0, R4.Pin_0
  GND: Part1.GND, U1.VSS, U1.R_W, U1.K, T1.GND, LED1.cathode, S1.Pin_3, S1.Pin_4, R1.leg2, RE1.EncoderPinC
  N12: U1.VO, R1.wiper
  N13: LED1.anode, R5.Pin_1
