# Fritzing sketch Yarn bath controller (saved by Fritzing 0.9.2b)
breadboards: 1

parts:
  Part1 = Photon
  Q1 = NPN-Transistor [package="TO92 [THT]"]
  R1 = Resistor [tolerance=±5% resistance=220 package=THT]

nets:
  N1: Part1.D0, R1.Pin_0
  N2: Q1.C, R1.Pin_1
